# Fritzing sketch ejemplo1-nodemcu (saved by Fritzing 0.9.9b)
breadboards: 1

parts:
  U1 = NodeMCU V3.0
  LED1 = smd LED [color="Red (633nm)" package="0805 [SMD]"]
  R1 = Resistor [tolerance=±5% resistance=220 package="0402 [SMD]"]

nets:
  N1: U1.D5, LED1.anode
  N2: U1.GND, R1.Pin_1
  N3: LED1.cathode, R1.Pin_0

custom parts:
  NodeMCU V3.0: NodeMcu V3 Lua WIFI Development Board
