# Fritzing sketch ejemplo2-nodemcu (saved by Fritzing 0.9.9b)
breadboards: 1

parts:
  U1 = NodeMCU V3.0
  RE1 = Rotary Encoder [package=THT]
  R1 = Resistor [tolerance=±5% power=0.25 resistance=220 package=THT]
  LED1 = LED - 5mm [color="Red (633nm)" current=0.030 package="5 mm [THT]"]

nets:
  N1: U1.3V3, RE1.EncoderPinB
  N2: U1.D7, LED1.anode
  N3: U1.A0, RE1.EncoderPinC
  N4: RE1.EncoderPinA, R1.Pin_1
  N5: R1.Pin_0, LED1.cathode

custom parts:
  NodeMCU V3.0: NodeMcu V3 Lua WIFI Development Board
