# Fritzing sketch ejemplo3-nodemcu (saved by Fritzing 0.9.9b)

parts:
  U1 = NodeMCU V3.0
  J1 = Basic Servo

nets:
  3V3: U1.3V3, J1.vcc

custom parts:
  NodeMCU V3.0: NodeMcu V3 Lua WIFI Development Board
